# Fritzing sketch Day4_One_LED (saved by Fritzing 1.0.6)
breadboards: 1

parts:
  A1 = Raspberry Pi Pico2
  R1 = Resistor [tolerance=±5% power=0.25W resistance=220 package=THT]
  LED1 = LED - 5mm [color="Red (633nm)" current=0.030A package="5 mm [THT]"]

nets:
  N1: A1.pin_3, A1.pin_8, A1.pin_13, A1.pin_18, A1.pin_23, A1.pin_28, A1.pin_33, A1.pin_38, LED1.cathode
  N2: A1.pin_20, R1.Pin_0
  N3: R1.Pin_1, LED1.anode

custom parts:
  Raspberry Pi Pico2: Raspberry Pi Pico 2 is our new $5 microcontroller board, built on RP2350: our new high-performance, secure microcontroller.
