# Fritzing sketch OneLEDSketch (saved by Fritzing 1.0.6)
breadboards: 1

parts:
  A1 = Raspberry Pi Pico2
  LED1 = LED - 5mm [color="Red (633nm)" current=0.030A package="5 mm [THT]"]
  R1 = Resistor [tolerance=±5% power=0.25W resistance=220 package=THT]

nets:
  N1: A1.pin_3, A1.pin_8, A1.pin_13, A1.pin_18, A1.pin_23, A1.pin_28, A1.pin_33, A1.pin_38, R1.Pin_1
  N2: A1.pin_20, LED1.anode
  N3: LED1.cathode, R1.Pin_0

custom parts:
  Raspberry Pi Pico2: Raspberry Pi Pico 2 is our new $5 microcontroller board, built on RP2350: our new high-performance, secure microcontroller.
