# Fritzing sketch pot (saved by Fritzing 1.0.6)
breadboards: 1

parts:
  A1 = Raspberry Pi Pico2
  R1 = Rotary Potentiometer (Small) [maximum_resistance=100kΩ knob_status=50% power=0.5W package=THT]

nets:
  N1: A1.pin_3, A1.pin_8, A1.pin_13, A1.pin_18, A1.pin_23, A1.pin_28, A1.pin_33, A1.pin_38, A1.pin_42, R1.leg2
  N2: A1.pin_31, R1.wiper
  N3: A1.pin_36, R1.leg1

custom parts:
  Raspberry Pi Pico2: Raspberry Pi Pico 2 is our new $5 microcontroller board, built on RP2350: our new high-performance, secure microcontroller.
